# Fritzing sketch B.ob_Wiring (saved by Fritzing 0.9.6b)
perfboards: 1

parts:
  ACT_BLDC-8015A-5_Right = IC, SIP package, 20 pins [chip_label=IC]
  ACT_BLDC-8015A-5_Left = IC, SIP package, 20 pins [chip_label=IC]
  Battery_20V = Power plug
  Buck-Converter = RioRand LM2596
  Raspberry_Pi_4B = Raspberry Pi 4B
  Right_Motor = SIP - 8 pins [package="SIP (Single Inline) [THT]"]
  Left_Motor = SIP - 8 pins [package="SIP (Single Inline) [THT]"]
  R2 = Resistor [tolerance=±5% power=0.25 resistance=220 package=THT]
  R3 = Resistor [tolerance=±5% power=0.25W resistance=1k package=THT]
  R1 = Resistor [tolerance=±5% power=0.25 resistance=220 package=THT]
  R4 = Resistor [tolerance=±5% power=0.25 resistance=1k package=THT]
  Q1 = MOSFET-NCHANNEL [package=sot23-3]
  R5 = Resistor [tolerance=±5% power=0.25 resistance=10k package=THT]
  R6 = Resistor [tolerance=±5% power=0.25 resistance=10k package=THT]
  Q2 = MOSFET-NCHANNEL [package=sot23-3]
  R7 = Resistor [tolerance=±5% power=0.25 resistance=10k package=THT]
  R8 = Resistor [tolerance=±5% power=0.25 resistance=10k package=THT]
  S1 = Round Pushbutton [part_number="Emergency Button"]
  LIDAR = RPlidar A1M8 [package=THT]
  U2 = Hirose DF13 Series Header [part_number="USB Adapter" package=DF13C-8P-1.25V]
  J1 = female pin header, 20 pins [form="♀ (female)" part_number=GND_CON]
  J3 = female pin header, 6 pins [form="♀ (female)" part_number=SDL_CON]
  J2 = female pin header, 6 pins [form="♀ (female)" part_number=SCL_CON]
  Part1 = InvenSense MPU6050 [part_number=IMU]
  USB-Hub = SIP - 5 pins [chip_label=USB-Hub package="SIP (Single Inline) [THT]"]
  USBTTL1 = USB A Plug
  USBTTL2 = USB B Plug
  USBTTL3 = USB A Plug
  USBTTL4 = USB B Plug
  U3 = SIP - 5 pins [chip_label=mmWave part_number=Rader package="SIP (Single Inline) [THT]"]

nets:
  GND: ACT_BLDC-8015A-5_Right.pin2, ACT_BLDC-8015A-5_Left.pin2, Raspberry_Pi_4B.GND, S1.leg1, J1.pin1, J1.pin2, J1.pin3, J1.pin4, J1.pin5, J1.pin6, J1.pin7, J1.pin8, J1.pin9, J1.pin10, J1.pin11, J1.pin12, J1.pin13, J1.pin14, J1.pin15, J1.pin16, J1.pin17, J1.pin18, J1.pin19, J1.pin20, Part1.GND, U3.GND
  RIGHT_ALM: ACT_BLDC-8015A-5_Right.pin3, Raspberry_Pi_4B.GPIO25, R2.Pin_1
  RIGHT_ENCODER: ACT_BLDC-8015A-5_Right.pin4, Raspberry_Pi_4B.GPIO24, R4.Pin_1
  RIGHT_PWM: ACT_BLDC-8015A-5_Right.pin5, Raspberry_Pi_4B.GPIO12
  LEFT_ENBL/RIGHT_ENBL: ACT_BLDC-8015A-5_Right.pin7, ACT_BLDC-8015A-5_Left.pin7, S1.leg0
  M_RIGHT_F/R: ACT_BLDC-8015A-5_Right.pin8, Q2.D, R8.Pin_1
  N1: ACT_BLDC-8015A-5_Right.pin9, Right_Motor.REF-
  N2: ACT_BLDC-8015A-5_Right.pin10, Right_Motor.HW
  N3: ACT_BLDC-8015A-5_Right.pin11, Right_Motor.HV
  N4: ACT_BLDC-8015A-5_Right.pin12, Right_Motor.HU
  N5: ACT_BLDC-8015A-5_Right.pin13, Right_Motor.REF+
  N6: ACT_BLDC-8015A-5_Right.pin16, ACT_BLDC-8015A-5_Left.pin16, Battery_20V.GND, Buck-Converter.Pin_2
  N7: ACT_BLDC-8015A-5_Right.pin17, ACT_BLDC-8015A-5_Left.pin17, Battery_20V.VCC, Buck-Converter.Pin_1
  N8: ACT_BLDC-8015A-5_Right.pin18, Right_Motor.U
  N9: ACT_BLDC-8015A-5_Right.pin19, Right_Motor.V
  N10: ACT_BLDC-8015A-5_Right.pin20, Right_Motor.W
  LEFT_ALM: ACT_BLDC-8015A-5_Left.pin3, Raspberry_Pi_4B.GPIO22, R1.Pin_1
  LEFT_ENCODER: ACT_BLDC-8015A-5_Left.pin4, Raspberry_Pi_4B.GPIO23, R3.Pin_1
  LEFT_PWM: ACT_BLDC-8015A-5_Left.pin5, Raspberry_Pi_4B.GPIO13
  M_LEFT_F/R: ACT_BLDC-8015A-5_Left.pin8, Q1.D, R7.Pin_1
  N11: ACT_BLDC-8015A-5_Left.pin9, Left_Motor.REF-
  N12: ACT_BLDC-8015A-5_Left.pin10, Left_Motor.HW
  N13: ACT_BLDC-8015A-5_Left.pin11, Left_Motor.HV
  N14: ACT_BLDC-8015A-5_Left.pin12, Left_Motor.HU
  N15: ACT_BLDC-8015A-5_Left.pin13, Left_Motor.REF+
  N16: ACT_BLDC-8015A-5_Left.pin18, Left_Motor.U
  N17: ACT_BLDC-8015A-5_Left.pin19, Left_Motor.V
  N18: ACT_BLDC-8015A-5_Left.pin20, Left_Motor.W
  Power_In: Buck-Converter.Pin_3, Buck-Converter.Pin_4, USBTTL2.pin1
  3.3V: Raspberry_Pi_4B.3V3, R2.Pin_0, R3.Pin_0, R1.Pin_0, R4.Pin_0, Q1.G, R5.Pin_0, R6.Pin_0, Q2.G, Part1.VCC, U3.3.3V
  5V: Raspberry_Pi_4B.5V, R7.Pin_0, R8.Pin_0
  SDL: Raspberry_Pi_4B.GPIO2, J3.pin1, J3.pin2, J3.pin3, J3.pin4, J3.pin5, J3.pin6, Part1.SDA
  SCL: Raspberry_Pi_4B.GPIO3, J2.pin1, J2.pin2, J2.pin3, J2.pin4, J2.pin5, J2.pin6, Part1.SCL
  Tx: Raspberry_Pi_4B.GPIO14, U3.Tx
  Rx: Raspberry_Pi_4B.GPIO15, U3.Rx
  LEFT_F/R: Raspberry_Pi_4B.GPIO6, Q1.S, R5.Pin_1
  RIGHT_F/R: Raspberry_Pi_4B.GPIO19, R6.Pin_1, Q2.S
  N19: LIDAR.pin1, U2.Tx
  N20: LIDAR.pin2, U2.Rx
  N21: LIDAR.pin3, U2.5V
  N22: LIDAR.pin4, U2.GND
  N23: LIDAR.pin5, U2.GND_MOTO
  N24: LIDAR.pin6, U2.CTRL_MOTO
  N25: LIDAR.pin7, U2.5V_MOTO
  OUTPUT_USB: U2.OUTPUT, USB-Hub.pin4, USBTTL3.usb, USBTTL4.pin1
  RPI_OUTPUT_USB-A: USB-Hub.input, USBTTL1.usb

notes:
  20V -> 5V
  Right_Motor
  Left_Motor
  default: closed
  IC1
  IC2
  D
  S
  G
  LIDAR

custom parts:
  SIP - 8 pins: A SIP stand-in part for whatever you want. With 8 pins on a 300 mil single inline package (SIP) footprint.
  RPlidar A1M8: .The RPLIDAR A1 is the next generation low cost 360 degree 2D laser scanner (LIDAR) solution developed by SLAMTEC. It can take up to 4000 samples of laser ranging per second with high rotation speed. And equipped with SLAMTEC patented OPTMAG technology, it breakouts the life limitation of traditional LIDAR system so as to work stably for a long time.
  Hirose DF13 Series Header: Hirose DF13 Header: 1.25mm Pitch Miniature Crimping Connector. Single Row Straight Pin Header (SMT)
  SIP - 5 pins: A SIP stand-in part for whatever you want. With 5 pins on a 300 mil single inline package (SIP) footprint.
  USB A Plug: USB A Plug breadboard only for documetnation purposes.
  USB B Plug: USB B Plug breadboard only for documetnation purposes.
  SIP - 5 pins: A SIP stand-in part for whatever you want. With 5 pins on a 300 mil single inline package (SIP) footprint.
